// Digital circuit Et + 1  2.dig as structural Verilog
module Et___1__2 (
  input  Et0,
  input  Et1,
  input  Et2,
  input  B,
  output Et_plus_1__2
);

  wire and_1_out, and_2_out, and_3_out, and_4_out;

  and and_1 (and_1_out, Et0, ~Et2, Et1);  // And
  and and_2 (and_2_out, B, Et0, ~Et2);  // And
  and and_3 (and_3_out, B, Et1, Et2);
  and and_4 (and_4_out, ~Et1, Et2, ~Et0);  // And
  or or_1 (Et_plus_1__2, and_1_out, and_2_out, and_3_out, and_4_out);
endmodule
