// Digital circuit Et + 1 1.dig as structural Verilog
module Et___1_1 (
  input  Et0,
  input  Et1,
  input  Et2,
  input  B,
  output Et__plus__1__1
);

  wire and_1_out, and_2_out, and_3_out;

  and and_1 (and_1_out, Et0, ~Et1, ~Et2);  // And
  and and_2 (and_2_out, ~Et0, ~Et2, Et1);  // And
  and and_3 (and_3_out, B, Et1, Et2);
  or or_1 (Et__plus__1__1, and_1_out, and_2_out, and_3_out);
endmodule
