// Digital circuit Et+1  0.dig as structural Verilog
module Et_1__0 (
  input  Et0,
  input  Et1,
  input  Et2,
  input  B,
  output Et_plus_1____0
);

  wire and_1_out, and_2_out, and_3_out;

  and and_1 (and_1_out, ~Et0, B);  // And
  and and_2 (and_2_out, ~Et0, ~Et2, Et1);  // And
  and and_3 (and_3_out, ~Et0, Et2, ~Et1);  // And
  or or_1 (Et_plus_1____0, and_1_out, and_2_out, and_3_out);
endmodule
