// Digital circuit resposta.dig as structural Verilog
module resposta (
  input  BOTAO,
  input  CLK,
  output SETA
);

  wire d_ff_1_q, d_ff_2_q, et_1__0_1_et_plus_1____0, et___1_1_1_et__plus__1__1, et___1__2_1_et_plus_1__2,
       rs_ff_as_1_q;

  RS_FF_AS rs_ff_as_1 (.S(BOTAO), .R(CLK), .Q(rs_ff_as_1_q));  // open: nQ
  Et___1__2 et___1__2_1 (
    .Et0(SETA), .Et1(d_ff_2_q), .Et2(d_ff_1_q), .B(rs_ff_as_1_q), .Et_plus_1__2(et___1__2_1_et_plus_1__2));
  Et___1_1 et___1_1_1 (
    .Et0(SETA), .Et1(d_ff_2_q), .Et2(d_ff_1_q), .B(rs_ff_as_1_q), .Et__plus__1__1(et___1_1_1_et__plus__1__1));
  Et_1__0 et_1__0_1 (
    .Et0(SETA), .Et1(d_ff_2_q), .Et2(d_ff_1_q), .B(rs_ff_as_1_q), .Et_plus_1____0(et_1__0_1_et_plus_1____0));
  D_FF d_ff_1 (.D(et___1__2_1_et_plus_1__2), .C(CLK), .Q(d_ff_1_q));  // open: nQ
  D_FF d_ff_2 (.D(et___1_1_1_et__plus__1__1), .C(CLK), .Q(d_ff_2_q));  // open: nQ
  D_FF d_ff_3 (.D(et_1__0_1_et_plus_1____0), .C(CLK), .Q(SETA));  // open: nQ
endmodule
